# Fritzing sketch project-x (saved by Fritzing 0.9.2b)
breadboards: 1

parts:
  Raspberry_Pi_B_rev1 = Raspberry Pi B rev1
  DHT1 = DHT11 Humitidy and Temperature Sensor
  KY-1 = Keyes Relay [package=THT]
  KY-2 = Keyes Relay [package=THT]
  R1 = Resistor [tolerance=±5% resistance=10k package="0805 [SMD]"]
  DHT2 = DHT11 Humitidy and Temperature Sensor
  U3 = BUTTON-CONDUCTIVE [package=button-conductive-0.1]  # not connected

nets:
  N1: Raspberry_Pi_B_rev1.3V3, DHT1.DATA, DHT1.NULL, R1.Pin_1, DHT2.NULL
  N2: Raspberry_Pi_B_rev1.5V, KY-1.power, KY-2.power
  GND: Raspberry_Pi_B_rev1.GND, DHT1.GND, KY-1.ground, KY-2.ground, DHT2.GND
  N3: Raspberry_Pi_B_rev1.GPIO_14, DHT2.DATA
  N4: Raspberry_Pi_B_rev1.GPIO_15, R1.Pin_0
  N5: Raspberry_Pi_B_rev1.GPIO_17, KY-1.signal
  N6: Raspberry_Pi_B_rev1.GPIO_22, KY-2.signal

custom parts:
  DHT11 Humitidy and Temperature Sensor: DHT11 Humidity and Temperature Sensor
  Keyes Relay: The Keyes 5V relay module is suitable for SCM development, home appliance control. It uses a 5V~12V TIL control signal which can control DC / AC signal.
